# Fritzing sketch irrigator (saved by Fritzing 0.9.3b)
breadboards: 1

parts:
  Raspberry_Pi_1 = Raspberry Pi 3 [part_number=RPI-3-V1.2]
  DHT1 = DHT11 Humitidy and Temperature Sensor
  IC1 = MCP3008 8-channel 10-bit ADC [part_number=MCP3008]
  Q1 = ULN2803 Darlington Array
  U1 = LM393 [package=so08]
  Part1 = Soil Moisture Sensor
  R1 = PHOTOCELL [package=photocell-kit]
  L1 = Solenoid
  L2 = Solenoid
  JACK1 = 2.1mm Barrel Jack with Terminal Block
  R2 = Resistor [tolerance=±5% resistance=100k package=THT]
  R4 = Resistor [tolerance=±5% resistance=10k package=THT]
  D1 = Rectifier Diode [part_number=1N4001 package="300 mil [THT]"]
  D2 = Rectifier Diode [part_number=1N4001 package="300 mil [THT]"]
  CLIP1 = Alligator Clip
  CLIP2 = Alligator Clip
  CLIP4 = Alligator Clip
  CLIP5 = Alligator Clip

nets:
  GND: Raspberry_Pi_1.GND, DHT1.GND, Q1.GND, U1.G1_-IN, R1.P$2, JACK1.NEG, R4.Pin_1
  N1: Raspberry_Pi_1.GPIO17, DHT1.DATA
  N2: Raspberry_Pi_1.GPIO10, IC1.no_name_yet#12
  N3: Raspberry_Pi_1.GPIO9, IC1.no_name_yet#13
  N4: Raspberry_Pi_1.GPIO11, IC1.no_name_yet#11
  N5: Raspberry_Pi_1.GPIO5, IC1.no_name_yet#10
  N6: Raspberry_Pi_1.GPIO24, Q1.I2
  N7: Raspberry_Pi_1.GPIO23, Q1.I1
  5V: Raspberry_Pi_1.5V, DHT1.VDD, IC1.no_name_yet#9, IC1.no_name_yet#14, IC1.no_name_yet#15, IC1.no_name_yet#16, U1.G1_OUT, R2.Pin_1
  N8: IC1.no_name_yet#1, U1.G1_V-
  N9: IC1.no_name_yet#2, R1.P$1, R2.Pin_0, R4.Pin_0
  N10: Q1.O2, L2.pin1
  N11: Q1.O1, L1.pin1
  N12: U1.G2_-IN, Part1.GND
  N13: U1.G2_OUT, Part1.VCC
  N14: JACK1.POS, D1.anode, D2.anode
  N15: CLIP1.wire, CLIP5.wire
  N16: CLIP2.wire, CLIP4.wire

notes:
  12V
  5V

custom parts:
  DHT11 Humitidy and Temperature Sensor: DHT11 Humidity and Temperature Sensor
  ULN2803 Darlington Array: ULN2803 Darlington Transistor Array with Flyback Protection
  Alligator Clip: Alligator clip
